# Fritzing sketch output-esp8266 (saved by Fritzing 0.9.3b)
breadboards: 1

parts:
  U1 = ESP8266 WiFi Module [part_number=ESP8266]
  Part1 = Arduino Uno (Rev3)
  DHT1 = DHT11 Humitidy and Temperature Sensor

nets:
  N1: U1.RXD, Part1.D0/RX
  VCC: U1.VCC, U1.CH_PD, Part1.3V3, DHT1.VDD
  GND: U1.GPIO_2, U1.GND, Part1.RESET, Part1.GND, DHT1.GND
  N2: U1.TXD, Part1.D1/TX
  N3: Part1.D2, DHT1.DATA

custom parts:
  ESP8266 WiFi Module: Generic WiFi Module based on the ESP8266 with onboard PCB antenna and UART communications
  DHT11 Humitidy and Temperature Sensor: DHT11 Humidity and Temperature Sensor
